# Fritzing sketch RF24SN-SparkCore (saved by Fritzing 0.9.0b)

parts:
  Part1 = Spark Core (v1.0)
  NRF24L1 = NRF24L01

nets:
  N1: Part1.A2, NRF24L1.CE
  N2: Part1.A3, NRF24L1.SCK
  N3: Part1.A4, NRF24L1.MISO
  N4: Part1.A5, NRF24L1.MOSI
  N5: Part1.D6, NRF24L1.CSN
  GND: Part1.GND, NRF24L1.GND
  3V3: Part1.3V3, NRF24L1.VCC

custom parts:
  NRF24L01: NRF24L01 module
